# Fritzing sketch FireTruck (saved by Fritzing 0.9.3b)

parts:
  Part1 = Bluetooth HC-05 Macho
  Part2 = Arduino Uno (Rev3)
  L298N2 = L298N DC motor driver
  M3 = DC Motor
  M4 = DC Motor
  U3 = LIPO-2000mAh [package=lipo-2000]
  U4 = LIPO-2000mAh [package=lipo-2000]

nets:
  N1: Part1.TXD, Part2.D10_PWM/SS
  N2: Part1.RXD, Part2.D11_PWM/MOSI
  N3: Part2.D2, L298N2.IN2
  N4: Part2.D3_PWM, L298N2.IN3
  N5: Part2.D4, L298N2.IN1
  N6: Part2.D5_PWM, L298N2.IN4
  N7: Part2.5V, L298N2.5V#7
  GND: Part2.GND, L298N2.GND, U3.-
  N8: L298N2.OUT1, M4.pin_2
  N9: L298N2.OUT2, M4.pin_1
  N10: L298N2.OUT3, M3.pin_2
  N11: L298N2.OUT4, M3.pin_1
  N12: L298N2.12V, U4.+
  N13: L298N2.5V#9, L298N2.ENA
  N14: L298N2.5V#10, L298N2.ENB
  N15: U3.+, U4.-

notes:
  L298N Motor Driver Board
  Left Right Motor
  Backward Forward Motor

custom parts:
  L298N DC motor driver: 2x DC motor driver with 78M05 positive voltage regulator (7..35 V) L298N: max 46 V, 2 A Set 5 V Enable jumper to enable 5 V regultor (needed for the L298N) and +5 V output at screw terminal or supply external +5 V at screw terminal Set ENA and/or ENB to +5 V to enable motor permanently or supply ENA and/or ENB with PWM signal IN1 and IN2 set rotation directory for motor A (OUT1/OUT2) IN2 and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
